# Fritzing sketch automatic-plant-watering (saved by Fritzing 0.9.3b)
perfboards: 1

parts:
  U1 = attiny85 [package=dip]
  LED1 = smd LED [color="Red (633nm)" package="1206 [SMD]"]
  R2 = Resistor [tolerance=±5% resistance=220 package=THT]
  LED2 = smd LED [color="Green (565nm)" package="1206 [SMD]"]
  R5 = Resistor [tolerance=±5% resistance=220 package=THT]
  R6 = Resistor [tolerance=±5% resistance=220 package=THT]
  LED3 = smd LED [color="Yellow (592nm)" package="1206 [SMD]"]
  R7 = Rotary Potentiometer (Small) [maximum_resistance=100kΩ package=THT]
  R8 = Rotary Potentiometer (Small) [maximum_resistance=100kΩ package=THT]
  S2 = Pushbutton [package=THT]
  R4 = Resistor [tolerance=±5% resistance=1M package=THT]
  KY-1 = Keyes Relay [package=THT]
  S3 = Pushbutton [package=THT]
  R9 = Resistor [tolerance=±5% resistance=1M package=THT]
  M1 = DC Motor  # not connected
  D1 = Rectifier Diode [part_number=1N4001 package="300 mil [THT]"]

nets:
  N1: U1.Pin_1, S2.leg0, R4.Pin_0
  N2: U1.Pin_2, R7.wiper
  N3: U1.Pin_3, R8.wiper
  N4: U1.Pin_5, S3.leg1, R9.Pin_0
  N5: U1.Pin_6, R6.Pin_1
  N6: U1.Pin_7, KY-1.signal
  N7: LED1.anode, R6.Pin_0
  N8: R2.Pin_0, LED2.anode
  N9: R5.Pin_0, LED3.anode
  N10: KY-1.NO, D1.cathode

custom parts:
  Keyes Relay: The Keyes 5V relay module is suitable for SCM development, home appliance control. It uses a 5V~12V TIL control signal which can control DC / AC signal.
